// Logisim project 8_draw_line.circ as structural Verilog: 3 circuits, main circuit main
module main (
  input  Load,
  input  EnableCounting,
  input  Reset,
  input  ResetMonitor,
  input  RefreshEnable,
  input  ResetRAM,
  input  [3:0] X1,
  input  [3:0] X2,
  input  WriteEnable,
  input  [7:0] color,
  input  [3:0] Y,
  output [7:0] OutputAddress
);

  wire and_1_out, clock_1_out, clock_2_out, comparator_1_lt, mmiosimulator_1_clocksignal,
       mmiosimulator_1_readsignal, mmiosimulator_1_writesignal, rgb_video_1_p1, rgb_video_1_p2,
       rgb_video_1_p3;
  wire [1:0] monitorcontrol_1_tosim;
  wire [3:0] rgb_video_1_p4, rgb_video_1_p5;
  wire [7:0] mmiosimulator_1_address, mmiosimulator_1_datatowrite, ram_1_dout, rgb_video_1_p6;
  wire [18:0] mmiosimulator_1_tomonitor;

  Comparator #(.mode("unsigned")) comparator_1 (.a(OutputAddress), .b({Y, X2}), .lt(comparator_1_lt));  // open: gt, eq
  and and_1 (and_1_out, EnableCounting, comparator_1_lt);
  Clock clock_1 (.out(clock_1_out));
  Counter counter_1 (
    .load(Load), .D({Y, X1}), .count(and_1_out), .Q(OutputAddress), .clk(clock_1_out), .clr(Reset));  // open: carry, up
  Clock clock_2 (.out(clock_2_out));
  // RGB_Video #(.cursor("No Cursor"), .height(16), .scale(8), .width(16)) rgb_video_1: pin names not known; wires that end beside it: rgb_video_1_p1, rgb_video_1_p2, rgb_video_1_p3, rgb_video_1_p4, rgb_video_1_p5, rgb_video_1_p6
  MonitorControl monitorcontrol_1 (
    .FromSim(mmiosimulator_1_tomonitor), .ResetScreen(ResetMonitor), .ScreenActivated(RefreshEnable),
    .ToSIM(monitorcontrol_1_tosim), .R(rgb_video_1_p1), .Clk(rgb_video_1_p2), .WE(rgb_video_1_p3),
    .X(rgb_video_1_p4), .Y(rgb_video_1_p5), .Col(rgb_video_1_p6));
  MMIOSimulator mmiosimulator_1 (
    .WriteData(color), .Clock(clock_2_out), .ReadData(ram_1_dout), .FromMonitor(monitorcontrol_1_tosim),
    .WriteEnable(WriteEnable), .WriteAddress(OutputAddress), .Address(mmiosimulator_1_address),
    .WriteSignal(mmiosimulator_1_writesignal), .ReadSignal(mmiosimulator_1_readsignal),
    .ClockSignal(mmiosimulator_1_clocksignal), .DataToWrite(mmiosimulator_1_datatowrite),
    .ToMonitor(mmiosimulator_1_tomonitor));
  RAM #(.asyncread("true"), .clearpin("true")) ram_1 (
    .addr(mmiosimulator_1_address), .we(mmiosimulator_1_writesignal), .oe(mmiosimulator_1_readsignal),
    .clk(mmiosimulator_1_clocksignal), .din(mmiosimulator_1_datatowrite), .dout(ram_1_dout), .clr(ResetRAM));
endmodule

module MonitorControl (
  input  ResetScreen,
  input  ScreenActivated,
  input  [18:0] FromSim,
  output [1:0] ToSIM,
  output R,
  output Clk,
  output WE,
  output [3:0] X,
  output [3:0] Y,
  output [7:0] Col
);


  assign Clk = FromSim[1];
  assign Col = FromSim[18:11];
  assign R = FromSim[0];
  assign ToSIM = {ScreenActivated, ResetScreen};
  assign WE = FromSim[2];
  assign X = FromSim[6:3];
  assign Y = FromSim[10:7];
endmodule

module MMIOSimulator (
  input  [1:0] FromMonitor,
  input  [7:0] WriteAddress,
  input  WriteEnable,
  input  [7:0] WriteData,
  input  Clock,
  input  [7:0] ReadData,
  output [7:0] Address,
  output WriteSignal,
  output ReadSignal,
  output [7:0] DataToWrite,
  output ClockSignal,
  output [18:0] ToMonitor
);

  wire and_1_out, and_2_out, and_3_out, buffer_1_out, buffer_2_out, buffer_3_out, buffer_4_out, buffer_5_out,
       buffer_6_out, not_1_out, xor_1_out;
  wire [7:0] controlled_buffer_3_out, counter_1_q, divider_1_out, divider_1_rem;

  Counter counter_1 (
    .count(FromMonitor[1]), .Q(counter_1_q), .clk(Clock), .clr(FromMonitor[0]));  // open: load, D, carry, up
  xor xor_1 (xor_1_out, Clock, ClockSignal);
  and and_1 (and_1_out, Clock, xor_1_out);
  buf buffer_1 (buffer_1_out, Clock);
  assign Address = and_1_out ? WriteAddress : 8'bz;  // Controlled_Buffer controlled_buffer_1
  and and_2 (and_2_out, and_1_out, WriteEnable);
  not not_1 (not_1_out, and_1_out);
  buf buffer_2 (buffer_2_out, buffer_5_out);
  buf buffer_3 (buffer_3_out, buffer_2_out);
  buf buffer_4 (buffer_4_out, buffer_1_out);
  buf buffer_5 (buffer_5_out, buffer_4_out);
  assign Address = not_1_out ? counter_1_q : 8'bz;  // Controlled_Buffer controlled_buffer_2
  buf buffer_6 (buffer_6_out, and_2_out);
  buf buffer_7 (WriteSignal, buffer_6_out);
  and and_3 (and_3_out, not_1_out, FromMonitor[1]);
  buf buffer_8 (ReadSignal, and_3_out);
  buf buffer_9 (ClockSignal, buffer_3_out);
  assign controlled_buffer_3_out = ReadSignal ? Address : 8'bz;  // Controlled_Buffer controlled_buffer_3
  Divider divider_1 (.a(controlled_buffer_3_out), .b(8'h10), .out(divider_1_out), .rem(divider_1_rem));  // open: upper
  Bit_Extender #(.out_width(4)) bit_extender_1 (.in(divider_1_out), .out(ToMonitor[10:7]));
  Bit_Extender #(.out_width(4)) bit_extender_2 (.in(divider_1_rem), .out(ToMonitor[6:3]));

  assign DataToWrite = WriteData;
  assign {ToMonitor[18:11], ToMonitor[2:0]} = {ReadData, FromMonitor[1], Clock, FromMonitor[0]};

  // Notes on the sheet:
  //   bit 0: reset screen
  //   bit 1: refresh activated
  //   ScreenReset
  //   ScreenClock
  //   ScreenWriteEnable
  //   ScreenX
  //   ScreenY
  //   ScreenColor
endmodule
